# Fritzing sketch BlinkNRF24L01 (saved by Fritzing 1.0.1rc)
breadboards: 1

parts:
  Componente1 = Arduino Uno (Rev3)
  Componente2 = Arduino Mega ADK (Rev3)
  Componente3 = NRF24L01+ Breakout Board
  Componente4 = NRF24L01+ Breakout Board
  Componente5 = NRF24L01+ Breakout Board
  U1 = attiny85 [package=dip]
  Componente6 = LilyPad Coin Cell Battery Holder

nets:
  Chip Enable: Componente1.D9_PWM, Componente4.CE
  Chip Select: Componente1.D10_PWM/SS, Componente4.CS
  MOSI: Componente1.D11_PWM/MOSI, Componente4.MOSI
  MISO: Componente1.D12/MISO, Componente4.MISO
  SCK: Componente1.D13/SCK, Componente4.SCK
  33V: Componente1.3V3, Componente2.3V3, Componente3.VCC, Componente4.VCC
  GND: Componente1.GND, Componente2.GND, Componente3.GND, Componente4.GND
  Chip Select MEGA: Componente2.D40, Componente3.CS
  Chip Enable MEGA: Componente2.D46, Componente3.CE
  MISO MEGA: Componente2.D50/MISO, Componente3.MISO
  MOSI MEGA: Componente2.D51/MOSI, Componente3.MOSI
  SCK MEGA: Componente2.D52/SCK, Componente3.SCK
  N1: Componente5.GND, U1.Pin_4, Componente6.-
  N2: Componente5.VCC, U1.Pin_8, Componente6.+
  Chip Enable Attiny: Componente5.CE, U1.Pin_2
  Chip Select Attiny: Componente5.CS, U1.Pin_3
  SCK Attiny: Componente5.SCK, U1.Pin_7
  MOSI Attiny: Componente5.MOSI, U1.Pin_5
  MISO Attiny: Componente5.MISO, U1.Pin_6

// code stored in the sketch: BlinkNRF24L01.ino
/*******************************************************************************************
Este é um projeto de "Hello World!" para testar os módulos de radiofrequencia NRF24L01
Baseado no próprios exemplos da biblioteca RF24 e o vídeo 
https://youtu.be/X7qWHlHh7DY?si=YLyKlsaAy6NsI5Ig do 
Prof. Cleber Borges do canal FunBots: https://www.youtube.com/@FunBots
******************************************************************************************


/******************************************************************************************
// Aqui começa o código para o Emissor que deve ser carregado apenas no Arduino Emissor
// ******************************************************************************************/


#include <RF24.h>


RF24 radio(9,10); // CE e CSN no arduino UNO - Arduino UNO atua como Emissor da mensagem apenas
const byte address[6] ="00001"; // ambos devem ter configurado o mesmo enderço para estabelecerem a comunicação



void setup() {
  radio.begin(); //Iniciamos comunicação via Radio
  radio.openWritingPipe(address); //Abrimos o Pipe de comunicação para escrita
  radio.setPALevel(RF24_PA_MIN); 
  /*Definimos o PA Level low para prevenir possíveis problmas de corrente
  dado que estes testes sáo realizados geralmente numa bancada com os rádios bem próximos.*/
  radio.stopListening(); // Este módulo apenas realizará o envio do Hello World, por tanto não precisa "escutar"
}
  


void loop() {
  const char text[] = "Hello World!"; // Criamos uma constante tipo texto para armazenar a mensagem que ser? enviada
  radio.write(&text, sizeof(text)); // Envia a mensagem de 
  delay(1000); // é um simples teste, então sim. Delay mesmo para simplificar.
}

/******************************************************************************************
// Aqui começa o código para o Receptor que deve ser carregado apenas no Arduino receptor
// ******************************************************************************************/


#include <RF24.h>


RF24 radio(46,40); // CE e CSN no arduno MEGA - Aduino Mega atua como receptor


const byte address[6] ="00001"; // ambos devem ter configurado o mesmo endere?o para estabelecerem a comunica??o


void setup() {
  Serial.begin(9600); // Iniciamos o Serial para podermos visualizar a mensagem
  Serial.print("Iniciando..."); 



  radio.begin(); //Iniciamos comunica??o via Radio
  radio.openReadingPipe(0, address); //Abrimos o Pipe de comunica??o para leitura
  radio.setPALevel(RF24_PA_MIN);
  /*Definimos o PA Level low para prevenir poss?veis problmas de corrente
  dado que estes testes s?o realizados geralmente numa bancada com os r?dios bem pr?ximos.*/
  radio.startListening(); // Este m?dulo apenas realizar? o recebimento da mensagem, por tanto n?o precisa "escutar"
}



void loop() {
  if(radio.available()){ //Verificamos que quando a mensagem tenha sido recebida, ele da True e executa o c?digo a seguir
    char text[32] = ""; // instancia uma vari?vel em branco
    radio.read(&text, sizeof(text)); //recebe a mensagem via radio e armazena na vari?vel text
    Serial.println(text);// imprime a vari?vel no terminal para podermos visualizar e validar que a comunica??o est? funcionando.
  }
}
